# Fritzing sketch current-warning (saved by Fritzing 0.8.7b)
breadboards: 1

parts:
  Part1 = Arduino Mega 2560 (Rev3)
  Q1 = MOSFET-NCHANNEL [package=to220v]
  Q2 = MOSFET-NCHANNEL [package=to220v]
  Q3 = MOSFET-NCHANNEL [package=to220v]
  LED1 = RGB LED (com. cathode, rgb) [package="5 mm [THT]"]
  U1 = LIPO-2000mAh [package=lipo-2000]
  S1 = Pushbutton [package="[THT]"]
  R1 = Resistor [tolerance=±5% resistance=10k package="0805 [SMD]"]
  R2 = Resistor [tolerance=±5% resistance=10k package="0805 [SMD]"]
  R3 = Resistor [tolerance=±5% resistance=10k package="0805 [SMD]"]
  R4 = Resistor [tolerance=±5% resistance=10k package="0805 [SMD]"]
  INA1 = INA219 DC Current Sensor Breakout
  M1 = DC Motor
  VCC1 = Battery  # not connected

nets:
  N1: Part1.D21/SCL, INA1.SCL
  N2: Part1.D20/SDA, INA1.SDA
  N3: Part1.D11_PWM, Q2.G, R3.Pin_0
  N4: Part1.D10_PWM, Q1.G, R2.Pin_0
  N5: Part1.D9_PWM, Q3.G, R1.Pin_0
  5V: Part1.5V, Part1.D52, S1.Pin_1, S1.Pin_2, INA1.VCC
  GND: Part1.GND, Q1.S, Q2.S, Q3.S, LED1.common_cathode, U1.-, R1.Pin_1, R3.Pin_1, R4.Pin_1, INA1.GND
  N6: Q1.D, LED1.green_anode
  N7: Q2.D, LED1.blue_anode
  N8: Q3.D, LED1.red_anode
  N9: S1.Pin_3, S1.Pin_4, R4.Pin_0
  N10: INA1.Vin-2, M1.pin_1, M1.pin_2

custom parts:
  INA219 DC Current Sensor Breakout: INA DC Current Sensor Breakout

// code stored in the sketch: current_monitor.ino
#include <Wire.h>
#include <Adafruit_INA219.h>

Adafruit_INA219 ina219;

//LED setup
int redPin = 9;
int greenPin = 10;
int bluePin = 11;

void setup(void) {
  uint32_t currentFrequency;
  Serial.begin(115200);
  Serial.println("Hello!");
  Serial.println("Measuring voltage and current with INA219 ...");
  ina219.begin();
}

void loop(void) {
  
  float current = 0;
  current = ina219.getCurrent_mA();
  Serial.print("Current Draw: ");
  Serial.println(current);
  
  if (current >= 1000) {
    /*LEDs Red*/
    digitalWrite(redPin, HIGH);
    digitalWrite(greenPin, LOW);
    digitalWrite(bluePin, LOW);
    delay(3000);
  } else {
    /*LEDs Purple*/
    digitalWrite(redPin, HIGH);
    digitalWrite(greenPin, LOW);
    digitalWrite(bluePin, HIGH);
  }
  
}
